// Logisim project micoX1.circ as structural Verilog: 13 circuits, main circuit main
module main (
  output [31:0] out_1,
  output [31:0] out_2
);

  wire B_IMED, clear, Clk, cond, DISPLAY, HALT, JUMP, multiplexer_1_out, not_1_out, W_E, ZeroULA;
  wire [2:0] ULAS;
  wire [31:0] bancoregistradores_1_saidaa, bancoregistradores_1_saidab, bit_extender_1_out,
       bit_extender_2_out, multiplexer_2_out, multiplexer_3_out, reg32bits_1_saida, rom_1_data,
       somadorlooka_1_result, ula_1_saida;

  Multiplexer multiplexer_1 (.in0(JUMP), .in1(ZeroULA), .out(multiplexer_1_out), .sel(cond));
  assign bit_extender_1_out = {{16{rom_1_data[31]}}, rom_1_data[31:16]};  // Bit_Extender bit_extender_1
  Multiplexer #(.width(32)) multiplexer_2 (
    .in0(32'h1), .in1(bit_extender_1_out), .out(multiplexer_2_out), .sel(multiplexer_1_out));
  SomadorLookA somadorlooka_1 (
    .A(multiplexer_2_out), .B(reg32bits_1_saida), .RESULT(somadorlooka_1_result));  // open: sub
  Reg32Bits reg32bits_1 (
    .Entrada(somadorlooka_1_result), .Enable(not_1_out), .Clk(Clk), .Clear(clear), .Saida(reg32bits_1_saida));
  not not_1 (not_1_out, HALT);
  ROM #(.addrWidth(7), .dataWidth(32)) rom_1 (.addr(reg32bits_1_saida[6:0]), .data(rom_1_data));
  Clock clock_1 (.out(Clk));
  Button button_1 (.out(clear));
  MEMORIA_CONTROLE memoria_controle_1 (
    .OPCODE(rom_1_data[3:0]), .COND(cond), .W_E(W_E), .DISPLAY(DISPLAY), .B_IMED(B_IMED), .JUMP(JUMP),
    .HALT(HALT), .OP_ULA(ULAS));
  assign bit_extender_2_out = {{16{rom_1_data[31]}}, rom_1_data[31:16]};  // Bit_Extender bit_extender_2
  BancoRegistradores bancoregistradores_1 (
    .B(rom_1_data[11:8]), .A(rom_1_data[7:4]), .in_2(clear), .in_1(Clk), .DadoEscrita(ula_1_saida),
    .C(rom_1_data[15:12]), .We(W_E), .SaidaB(bancoregistradores_1_saidab),
    .SaidaA(bancoregistradores_1_saidaa));
  Multiplexer #(.width(32)) multiplexer_3 (
    .in0(bancoregistradores_1_saidab), .in1(bit_extender_2_out), .out(multiplexer_3_out), .sel(B_IMED));
  Reg32Bits reg32bits_2 (
    .Entrada(bancoregistradores_1_saidaa), .Enable(DISPLAY), .Clk(Clk), .Clear(clear), .Saida(out_1));
  ULA ula_1 (
    .Seletor(ULAS), .in_2(multiplexer_3_out), .in_1(bancoregistradores_1_saidaa), .Saida(ula_1_saida),
    .ZERO(ZeroULA));

  assign out_2 = out_1;

  // Notes on the sheet:
  //   contents of rom_1 (hex, n*v repeats v):
  //   5100b 1c 1a00b cba1 bc ffff101b b0ab a0cb 2010e fffa000d f
endmodule

module MEMORIA_CONTROLE (
  input  [3:0] OPCODE,
  output [2:0] OP_ULA,
  output COND,
  output W_E,
  output DISPLAY,
  output B_IMED,
  output JUMP,
  output HALT
);

  ROM #(.addrWidth(4), .dataWidth(9)) rom_1 (.addr(OPCODE), .data({HALT, JUMP, B_IMED, DISPLAY, W_E, COND, OP_ULA}));

  // Notes on the sheet:
  //   contents of rom_1 (hex, n*v repeats v):
  //   0 10 11 12 13 14 15 16 17 53 54 50 20 80 9 100
endmodule

module SomadorUmBit (
  input  in_1,
  input  in_2,
  input  C_in,
  output R
);

  wire xor_1_out;

  xor xor_1 (xor_1_out, in_1, in_2);
  xor xor_2 (R, xor_1_out, C_in);
endmodule

module SomadorLookA (
  input  [31:0] B,
  input  [31:0] A,
  input  sub,
  output [31:0] RESULT
);

  wire lookahead4bits_1_c_out, lookahead4bits_2_c_out, lookahead4bits_3_c_out, lookahead4bits_4_c_out,
       lookahead4bits_5_c_out, lookahead4bits_6_c_out, lookahead4bits_7_c_out;
  wire [3:0] B1, B2, B3, B4, B5, B6, B7, B8;
  wire [31:0] not_1_out;

  assign not_1_out = ~B;  // NOT_Gate not_1, 32 bits wide
  Multiplexer #(.width(32)) multiplexer_1 (.in0(B), .in1(not_1_out), .out({B8, B7, B6, B5, B4, B3, B2, B1}), .sel(sub));
  LookAhead4Bits lookahead4bits_1 (
    .C_in(sub), .A(A[3:0]), .B(B1), .C_out(lookahead4bits_1_c_out), .result(RESULT[3:0]));
  LookAhead4Bits lookahead4bits_2 (
    .C_in(lookahead4bits_5_c_out), .A(A[11:8]), .B(B3), .C_out(lookahead4bits_2_c_out), .result(RESULT[11:8]));
  LookAhead4Bits lookahead4bits_3 (
    .C_in(lookahead4bits_6_c_out), .A(A[19:16]), .B(B5), .C_out(lookahead4bits_3_c_out),
    .result(RESULT[19:16]));
  LookAhead4Bits lookahead4bits_4 (
    .C_in(lookahead4bits_7_c_out), .A(A[27:24]), .B(B7), .C_out(lookahead4bits_4_c_out),
    .result(RESULT[27:24]));
  LookAhead4Bits lookahead4bits_5 (
    .C_in(lookahead4bits_1_c_out), .A(A[7:4]), .B(B2), .C_out(lookahead4bits_5_c_out), .result(RESULT[7:4]));
  LookAhead4Bits lookahead4bits_6 (
    .C_in(lookahead4bits_2_c_out), .A(A[15:12]), .B(B4), .C_out(lookahead4bits_6_c_out),
    .result(RESULT[15:12]));
  LookAhead4Bits lookahead4bits_7 (
    .C_in(lookahead4bits_3_c_out), .A(A[23:20]), .B(B6), .C_out(lookahead4bits_7_c_out),
    .result(RESULT[23:20]));
  LookAhead4Bits lookahead4bits_8 (
    .C_in(lookahead4bits_4_c_out), .A(A[31:28]), .B(B8), .result(RESULT[31:28]));  // open: C_out

  // Other names for the same wires on the sheet: A1[3:0] = A[3:0]; A2[3:0] = A[7:4]; A3[3:0] = A[11:8];
  //   A4[3:0] = A[15:12]; A5[3:0] = A[19:16]; A6[3:0] = A[23:20]; A7[3:0] = A[27:24]; A8[3:0] = A[31:28];
  //   S1[3:0] = RESULT[3:0]; S2[3:0] = RESULT[7:4]; S3[3:0] = RESULT[11:8]; S4[3:0] = RESULT[15:12];
  //   S5[3:0] = RESULT[19:16]; S6[3:0] = RESULT[23:20]; S7[3:0] = RESULT[27:24]; S8[3:0] = RESULT[31:28]; sub_t = sub
endmodule

module SistemaLA4bits (
  input  A3,
  input  A2,
  input  B3,
  input  A1,
  input  B2,
  input  A0,
  input  B1,
  input  B0,
  input  C0,
  output C4,
  output C3,
  output C2,
  output C1
);

  wire and_1_out, and_2_out, and_3_out, and_4_out, and_5_out, and_6_out, and_7_out, and_8_out, or_1_out,
       or_3_out, or_4_out, or_7_out;

  or or_1 (or_1_out, B0, A0);
  and and_1 (and_1_out, B0, A0);
  and and_2 (and_2_out, or_1_out, C0);
  or or_2 (C1, and_1_out, and_2_out);
  or or_3 (or_3_out, B1, A1);
  and and_3 (and_3_out, or_3_out, C1);
  and and_4 (and_4_out, B1, A1);
  or or_4 (or_4_out, B2, A2);
  or or_5 (C2, and_4_out, and_3_out);
  and and_5 (and_5_out, or_4_out, C2);
  and and_6 (and_6_out, B2, A2);
  or or_6 (C3, and_6_out, and_5_out);
  or or_7 (or_7_out, B3, A3);
  and and_7 (and_7_out, B3, A3);
  and and_8 (and_8_out, or_7_out, C3);
  or or_8 (C4, and_7_out, and_8_out);
endmodule

module LookAhead4Bits (
  input  [3:0] B,
  input  [3:0] A,
  input  C_in,
  output C_out,
  output [3:0] result
);

  wire sistemala4bits_1_c1, sistemala4bits_1_c2, sistemala4bits_1_c3;

  SomadorUmBit somadorumbit_1 (.in_1(A[0]), .in_2(B[0]), .C_in(C_in), .R(result[0]));
  SistemaLA4bits sistemala4bits_1 (
    .A0(A[0]), .B0(B[0]), .C0(C_in), .A1(A[1]), .B1(B[1]), .A2(A[2]), .B2(B[2]), .A3(A[3]), .B3(B[3]),
    .C4(C_out), .C1(sistemala4bits_1_c1), .C2(sistemala4bits_1_c2), .C3(sistemala4bits_1_c3));
  SomadorUmBit somadorumbit_2 (.in_1(A[1]), .in_2(B[1]), .C_in(sistemala4bits_1_c1), .R(result[1]));
  SomadorUmBit somadorumbit_3 (.in_1(A[2]), .in_2(B[2]), .C_in(sistemala4bits_1_c2), .R(result[2]));
  SomadorUmBit somadorumbit_4 (.in_1(A[3]), .in_2(B[3]), .C_in(sistemala4bits_1_c3), .R(result[3]));
endmodule

module ULA (
  input  [31:0] in_1,
  input  [31:0] in_2,
  input  [2:0] Seletor,
  output ZERO,
  output [31:0] Saida
);

  wire scanshift_1_saida;
  wire [31:0] AND32_out, lshifter_1_b, NOT_A_out, OR32_out, rshifter_1_b, somadorlooka_1_result,
       somadorlooka_2_result, XOR32_out;

  SomadorLookA somadorlooka_1 (.A(in_1), .B(in_2), .sub(1'b0), .RESULT(somadorlooka_1_result));
  SomadorLookA somadorlooka_2 (.A(in_1), .B(in_2), .sub(1'b1), .RESULT(somadorlooka_2_result));
  assign AND32_out = in_1 & in_2;  // AND_Gate AND32, 32 bits wide
  assign OR32_out = in_1 | in_2;  // OR_Gate OR32, 32 bits wide
  Multiplexer #(.select(3), .width(32)) multiplexer_1 (
    .in0(somadorlooka_1_result), .in1(somadorlooka_2_result), .in2(AND32_out), .in3(OR32_out),
    .in4(XOR32_out), .in5(NOT_A_out), .in6(lshifter_1_b), .in7(rshifter_1_b), .out(Saida), .sel(Seletor));
  assign XOR32_out = in_1 ^ in_2;  // XOR_Gate XOR32, 32 bits wide
  assign NOT_A_out = ~in_1;  // NOT_Gate NOT_A, 32 bits wide
  ScanSHIFT scanshift_1 (
    .in10(Saida[9:5]), .in11(Saida[14:10]), .in12(Saida[19:15]), .in20(Saida[23:20]), .in21(Saida[27:24]),
    .in22(Saida[31:28]), .saida(scanshift_1_saida));
  LShifter lshifter_1 (.Shift(in_2), .A(in_1), .B(lshifter_1_b));
  nor nor_1 (ZERO, Saida[0], Saida[1], Saida[2], Saida[3], Saida[4], scanshift_1_saida);
  RShifter rshifter_1 (.Shift(in_2), .A(in_1), .B(rshifter_1_b));
endmodule

module ScanSHIFT (
  input  [4:0] in10,
  input  [4:0] in11,
  input  [4:0] in12,
  input  [3:0] in20,
  input  [3:0] in21,
  input  [3:0] in22,
  output saida
);

  wire or_1_out, or_2_out, or_3_out, or_4_out, or_5_out, or_6_out;

  or or_1 (or_1_out, in10[0], in10[1], in10[2], in10[3], in10[4]);
  or or_2 (or_2_out, in11[0], in11[1], in11[2], in11[3], in11[4]);
  or or_3 (or_3_out, in12[0], in12[1], in12[2], in12[3], in12[4]);
  or or_4 (or_4_out, in20[0], in20[1], in20[2], in20[3]);
  or or_5 (or_5_out, in21[0], in21[1], in21[2], in21[3]);
  or or_6 (or_6_out, in22[0], in22[1], in22[2], in22[3]);
  or or_7 (saida, or_1_out, or_2_out, or_3_out, or_4_out, or_5_out, or_6_out);
endmodule

module SD (
  input  [3:0] Entrada,
  input  Const,
  input  seletor,
  output PrevBit,
  output [3:0] Saida
);

  Multiplexer multiplexer_1 (.in0(Entrada[3]), .in1(Const), .out(Saida[3]), .sel(seletor));
  Multiplexer multiplexer_2 (.in0(Entrada[0]), .in1(Entrada[1]), .out(Saida[0]), .sel(seletor));
  Multiplexer multiplexer_3 (.in0(Entrada[1]), .in1(Entrada[2]), .out(Saida[1]), .sel(seletor));
  Multiplexer multiplexer_4 (.in0(Entrada[2]), .in1(Entrada[3]), .out(Saida[2]), .sel(seletor));

  assign PrevBit = Entrada[0];
endmodule

module Reg32Bits (
  input  [31:0] Entrada,
  input  Enable,
  input  Clk,
  input  Clear,
  output [31:0] Saida
);

  wire E_0, E_1, E_2, E_3, E_4, E_5, E_6, E_7, E_8, E_9, E_10, E_11, E_12, E_13, E_14, E_15, E_16, E_17,
       E_18, E_19, E_20, E_21, E_22, E_23, E_24, E_25, E_26, E_27, E_28, E_29, E_30, E_31;

  Multiplexer #(.width(32)) multiplexer_1 (
    .in1(Entrada),
    .out({E_31, E_30, E_29, E_28, E_27, E_26, E_25, E_24, E_23, E_22, E_21, E_20, E_19, E_18, E_17, E_16, E_15, E_14, E_13, E_12, E_11, E_10, E_9, E_8, E_7, E_6, E_5, E_4, E_3, E_2, E_1, E_0}),
    .sel(Enable));  // open: in0
  D_Flip_Flop d_ff_1 (.D(E_0), .clk(Clk), .Q(Saida[0]), .reset(Clear));  // open: Qn, preset
  D_Flip_Flop d_ff_2 (.D(E_8), .clk(Clk), .Q(Saida[8]), .reset(Clear));  // open: Qn, preset
  D_Flip_Flop d_ff_3 (.D(E_16), .clk(Clk), .Q(Saida[16]), .reset(Clear));  // open: Qn, preset
  D_Flip_Flop d_ff_4 (.D(E_24), .clk(Clk), .Q(Saida[24]), .reset(Clear));  // open: Qn, preset
  D_Flip_Flop d_ff_5 (.D(E_1), .clk(Clk), .Q(Saida[1]), .reset(Clear));  // open: Qn, preset
  D_Flip_Flop d_ff_6 (.D(E_9), .clk(Clk), .Q(Saida[9]), .reset(Clear));  // open: Qn, preset
  D_Flip_Flop d_ff_7 (.D(E_17), .clk(Clk), .Q(Saida[17]), .reset(Clear));  // open: Qn, preset
  D_Flip_Flop d_ff_8 (.D(E_25), .clk(Clk), .Q(Saida[25]), .reset(Clear));  // open: Qn, preset
  D_Flip_Flop d_ff_9 (.D(E_2), .clk(Clk), .Q(Saida[2]), .reset(Clear));  // open: Qn, preset
  D_Flip_Flop d_ff_10 (.D(E_10), .clk(Clk), .Q(Saida[10]), .reset(Clear));  // open: Qn, preset
  D_Flip_Flop d_ff_11 (.D(E_18), .clk(Clk), .Q(Saida[18]), .reset(Clear));  // open: Qn, preset
  D_Flip_Flop d_ff_12 (.D(E_26), .clk(Clk), .Q(Saida[26]), .reset(Clear));  // open: Qn, preset
  D_Flip_Flop d_ff_13 (.D(E_3), .clk(Clk), .Q(Saida[3]), .reset(Clear));  // open: Qn, preset
  D_Flip_Flop d_ff_14 (.D(E_11), .clk(Clk), .Q(Saida[11]), .reset(Clear));  // open: Qn, preset
  D_Flip_Flop d_ff_15 (.D(E_19), .clk(Clk), .Q(Saida[19]), .reset(Clear));  // open: Qn, preset
  D_Flip_Flop d_ff_16 (.D(E_27), .clk(Clk), .Q(Saida[27]), .reset(Clear));  // open: Qn, preset
  D_Flip_Flop d_ff_17 (.D(E_4), .clk(Clk), .Q(Saida[4]), .reset(Clear));  // open: Qn, preset
  D_Flip_Flop d_ff_18 (.D(E_12), .clk(Clk), .Q(Saida[12]), .reset(Clear));  // open: Qn, preset
  D_Flip_Flop d_ff_19 (.D(E_20), .clk(Clk), .Q(Saida[20]), .reset(Clear));  // open: Qn, preset
  D_Flip_Flop d_ff_20 (.D(E_28), .clk(Clk), .Q(Saida[28]), .reset(Clear));  // open: Qn, preset
  D_Flip_Flop d_ff_21 (.D(E_5), .clk(Clk), .Q(Saida[5]), .reset(Clear));  // open: Qn, preset
  D_Flip_Flop d_ff_22 (.D(E_13), .clk(Clk), .Q(Saida[13]), .reset(Clear));  // open: Qn, preset
  D_Flip_Flop d_ff_23 (.D(E_21), .clk(Clk), .Q(Saida[21]), .reset(Clear));  // open: Qn, preset
  D_Flip_Flop d_ff_24 (.D(E_29), .clk(Clk), .Q(Saida[29]), .reset(Clear));  // open: Qn, preset
  D_Flip_Flop d_ff_25 (.D(E_6), .clk(Clk), .Q(Saida[6]), .reset(Clear));  // open: Qn, preset
  D_Flip_Flop d_ff_26 (.D(E_7), .clk(Clk), .Q(Saida[7]), .reset(Clear));  // open: Qn, preset
  D_Flip_Flop d_ff_27 (.D(E_14), .clk(Clk), .Q(Saida[14]), .reset(Clear));  // open: Qn, preset
  D_Flip_Flop d_ff_28 (.D(E_22), .clk(Clk), .Q(Saida[22]), .reset(Clear));  // open: Qn, preset
  D_Flip_Flop d_ff_29 (.D(E_30), .clk(Clk), .Q(Saida[30]), .reset(Clear));  // open: Qn, preset
  D_Flip_Flop d_ff_30 (.D(E_15), .clk(Clk), .Q(Saida[15]), .reset(Clear));  // open: Qn, preset
  D_Flip_Flop d_ff_31 (.D(E_23), .clk(Clk), .Q(Saida[23]), .reset(Clear));  // open: Qn, preset
  D_Flip_Flop d_ff_32 (.D(E_31), .clk(Clk), .Q(Saida[31]), .reset(Clear));  // open: Qn, preset

  // Other names for the same wires on the sheet: S_0 = Saida[0]; S_1 = Saida[1]; S_2 = Saida[2]; S_3 = Saida[3];
  //   S_4 = Saida[4]; S_5 = Saida[5]; S_6 = Saida[6]; S_7 = Saida[7]; S_8 = Saida[8]; S_9 = Saida[9];
  //   S_10 = Saida[10]; S_11 = Saida[11]; S_12 = Saida[12]; S_13 = Saida[13]; S_14 = Saida[14]; S_15 = Saida[15];
  //   S_16 = Saida[16]; S_17 = Saida[17]; S_18 = Saida[18]; S_19 = Saida[19]; S_20 = Saida[20]; S_21 = Saida[21];
  //   S_22 = Saida[22]; S_23 = Saida[23]; S_24 = Saida[24]; S_25 = Saida[25]; S_26 = Saida[26]; S_27 = Saida[27];
  //   S_28 = Saida[28]; S_29 = Saida[29]; S_30 = Saida[30]; S_31 = Saida[31]
endmodule

module LShifter (
  input  [31:0] A,
  input  [31:0] Shift,
  output [31:0] B
);

  wire or_1_out;
  wire [31:0] multiplexer_1_out, multiplexer_2_out, multiplexer_4_out, multiplexer_5_out;
  wire [31:8] multiplexer_3_out_2;
  wire [31:24] multiplexer_3_out;

  or or_1 (or_1_out, Shift[5], Shift[6], Shift[7], Shift[8], Shift[9], Shift[10], Shift[11], Shift[12], Shift[13], Shift[14], Shift[15], Shift[16], Shift[17], Shift[18], Shift[19], Shift[20], Shift[21], Shift[22], Shift[23], Shift[24], Shift[25], Shift[26], Shift[27], Shift[28], Shift[29], Shift[30], Shift[31]);
  Multiplexer #(.width(32)) multiplexer_1 (.in0(A), .in1({A[30:0], 1'b0}), .out(multiplexer_1_out), .sel(Shift[0]));
  Multiplexer #(.width(32)) multiplexer_2 (
    .in0(multiplexer_1_out), .in1({multiplexer_1_out[29:0], 2'b00}), .out(multiplexer_2_out), .sel(Shift[1]));
  Multiplexer #(.width(32)) multiplexer_3 (
    .in0(multiplexer_2_out), .in1({multiplexer_2_out[27:0], 4'b0000}),
    .out({multiplexer_3_out, multiplexer_3_out_2}), .sel(Shift[2]));
  Multiplexer #(.width(32)) multiplexer_4 (
    .in0({multiplexer_3_out, multiplexer_3_out_2}), .in1({multiplexer_3_out_2, {8{1'b0}}}),
    .out(multiplexer_4_out), .sel(Shift[3]));
  Multiplexer #(.width(32)) multiplexer_5 (
    .in0(multiplexer_4_out), .in1({multiplexer_4_out[15:0], {16{1'b0}}}), .out(multiplexer_5_out),
    .sel(Shift[4]));
  Multiplexer #(.width(32)) multiplexer_6 (.in0(multiplexer_5_out), .in1({32{1'b0}}), .out(B), .sel(or_1_out));
endmodule

module BancoRegistradores (
  input  in_1,
  input  in_2,
  input  [31:0] DadoEscrita,
  input  [3:0] A,
  input  [3:0] C,
  input  We,
  input  [3:0] B,
  output [31:0] SaidaA,
  output [31:0] SaidaB
);

  wire w1, w2, w3, w4, w5, w6, w7, w8, w9, w10, w11, w12, w13, w14, w15, w16;
  wire [31:0] BD1, BD2, BD3, BD4, BD5, BD6, BD7, BD8, BD9, BD10, BD11, BD12, BD13, BD14, BD15, BD16, S1, S2,
       S3, S4, S5, S6, S7, S8, S9, S10, S11, S12, S13, S14, S15, S16;

  Multiplexer #(.select(4), .width(32)) multiplexer_1 (
    .in0(S1), .in1(S2), .in2(S3), .in3(S4), .in4(S5), .in5(S6), .in6(S7), .in7(S8), .in8(S9), .in9(S10),
    .in10(S11), .in11(S12), .in12(S13), .in13(S14), .in14(S15), .in15(S16), .out(SaidaA), .sel(A));
  Multiplexer #(.select(4), .width(32)) multiplexer_2 (
    .in0(S1), .in1(S2), .in2(S3), .in3(S4), .in4(S5), .in5(S6), .in6(S7), .in7(S8), .in8(S9), .in9(S10),
    .in10(S11), .in11(S12), .in12(S13), .in13(S14), .in14(S15), .in15(S16), .out(SaidaB), .sel(B));
  Demultiplexer #(.select(4), .width(32)) demultiplexer_1 (
    .out0(BD1), .out1(BD2), .out2(BD3), .out3(BD4), .out4(BD5), .out5(BD6), .out6(BD7), .out7(BD8),
    .out8(BD9), .out9(BD10), .out10(BD11), .out11(BD12), .out12(BD13), .out13(BD14), .out14(BD15),
    .out15(BD16), .in(DadoEscrita), .sel(C));
  Demultiplexer #(.select(4)) demultiplexer_2 (
    .out0(w1), .out1(w2), .out2(w3), .out3(w4), .out4(w5), .out5(w6), .out6(w7), .out7(w8), .out8(w9),
    .out9(w10), .out10(w11), .out11(w12), .out12(w13), .out13(w14), .out14(w15), .out15(w16), .in(We), .sel(C));
  Reg32Bits reg32bits_1 (.Entrada(BD1), .Enable(w1), .Clk(in_1), .Clear(in_2), .Saida(S1));
  Reg32Bits reg32bits_2 (.Entrada(BD5), .Enable(w5), .Clk(in_1), .Clear(in_2), .Saida(S5));
  Reg32Bits reg32bits_3 (.Entrada(BD9), .Enable(w9), .Clk(in_1), .Clear(in_2), .Saida(S9));
  Reg32Bits reg32bits_4 (.Entrada(BD13), .Enable(w13), .Clk(in_1), .Clear(in_2), .Saida(S13));
  Reg32Bits reg32bits_5 (.Entrada(BD2), .Enable(w2), .Clk(in_1), .Clear(in_2), .Saida(S2));
  Reg32Bits reg32bits_6 (.Entrada(BD6), .Enable(w6), .Clk(in_1), .Clear(in_2), .Saida(S6));
  Reg32Bits reg32bits_7 (.Entrada(BD10), .Enable(w10), .Clk(in_1), .Clear(in_2), .Saida(S10));
  Reg32Bits reg32bits_8 (.Entrada(BD14), .Enable(w14), .Clk(in_1), .Clear(in_2), .Saida(S14));
  Reg32Bits reg32bits_9 (.Entrada(BD3), .Enable(w3), .Clk(in_1), .Clear(in_2), .Saida(S3));
  Reg32Bits reg32bits_10 (.Entrada(BD7), .Enable(w7), .Clk(in_1), .Clear(in_2), .Saida(S7));
  Reg32Bits reg32bits_11 (.Entrada(BD11), .Enable(w11), .Clk(in_1), .Clear(in_2), .Saida(S11));
  Reg32Bits reg32bits_12 (.Entrada(BD15), .Enable(w15), .Clk(in_1), .Clear(in_2), .Saida(S15));
  Reg32Bits reg32bits_13 (.Entrada(BD4), .Enable(w4), .Clk(in_1), .Clear(in_2), .Saida(S4));
  Reg32Bits reg32bits_14 (.Entrada(BD8), .Enable(w8), .Clk(in_1), .Clear(in_2), .Saida(S8));
  Reg32Bits reg32bits_15 (.Entrada(BD12), .Enable(w12), .Clk(in_1), .Clear(in_2), .Saida(S12));
  Reg32Bits reg32bits_16 (.Entrada(BD16), .Enable(w16), .Clk(in_1), .Clear(in_2), .Saida(S16));

  // Other names for the same wires on the sheet: Clear = in_2; Clk = in_1
endmodule

module RShifter (
  input  [31:0] A,
  input  [31:0] Shift,
  output [31:0] B
);

  wire or_1_out;
  wire [31:0] multiplexer_1_out, multiplexer_2_out, multiplexer_4_out, multiplexer_5_out;
  wire [31:8] multiplexer_3_out_2;
  wire [31:24] multiplexer_3_out;

  or or_1 (or_1_out, Shift[0], Shift[1], Shift[2], Shift[3], Shift[4], Shift[5], Shift[6], Shift[7], Shift[8], Shift[9], Shift[10], Shift[11], Shift[12], Shift[13], Shift[14], Shift[15], Shift[16], Shift[17], Shift[18], Shift[19], Shift[20], Shift[21], Shift[22], Shift[23], Shift[24], Shift[25], Shift[26]);
  Multiplexer #(.width(32)) multiplexer_1 (.in0(A), .in1({A[30:0], 1'b0}), .out(multiplexer_1_out), .sel(Shift[31]));
  Multiplexer #(.width(32)) multiplexer_2 (
    .in0(multiplexer_1_out), .in1({multiplexer_1_out[29:0], 2'b00}), .out(multiplexer_2_out), .sel(Shift[30]));
  Multiplexer #(.width(32)) multiplexer_3 (
    .in0(multiplexer_2_out), .in1({multiplexer_2_out[27:0], 4'b0000}),
    .out({multiplexer_3_out, multiplexer_3_out_2}), .sel(Shift[29]));
  Multiplexer #(.width(32)) multiplexer_4 (
    .in0({multiplexer_3_out, multiplexer_3_out_2}), .in1({multiplexer_3_out_2, {8{1'b0}}}),
    .out(multiplexer_4_out), .sel(Shift[28]));
  Multiplexer #(.width(32)) multiplexer_5 (
    .in0(multiplexer_4_out), .in1({multiplexer_4_out[15:0], {16{1'b0}}}), .out(multiplexer_5_out),
    .sel(Shift[27]));
  Multiplexer #(.width(32)) multiplexer_6 (.in0(multiplexer_5_out), .in1({32{1'b0}}), .out(B), .sel(or_1_out));
endmodule
